// Logisim project project.circ as structural Verilog: 1 circuit, main circuit main
module main (
);


  // Notes on the sheet:
  //   Deigo Castillo
  //   Team: Rizz Overflow
  //   Sergio Najm
endmodule
